// Logisim project logism_design.circ as structural Verilog
module half_adder (
  input  A,
  input  B,
  output out_3,
  output out_4
);

  xor xor_1 (out_3, A, B);
  and and_1 (out_4, A, B);
endmodule

module full_adder (
  input  in_1,
  input  in_2,
  input  in_3,
  output out_4,
  output out_5
);

  wire and_1_out, and_2_out, xor_1_out;

  xor xor_1 (xor_1_out, in_1, in_2);
  xor xor_2 (out_4, xor_1_out, in_3);
  and and_1 (and_1_out, xor_1_out, in_3);
  and and_2 (and_2_out, in_2, in_1);
  or or_1 (out_5, and_1_out, and_2_out);
endmodule

module _2bit_adder (
  input  [1:0] A,
  input  [1:0] B,
  input  C,
  output [1:0] sum,
  output out_5
);

  wire full_adder_1_out_5;

  full_adder full_adder_1 (.in_1(A[0]), .in_2(B[0]), .in_3(C), .out_4(sum[0]), .out_5(full_adder_1_out_5));
  full_adder full_adder_2 (.in_1(A[1]), .in_2(B[1]), .in_3(full_adder_1_out_5), .out_4(sum[1]), .out_5(out_5));
endmodule
